# Fritzing sketch schema (saved by Fritzing 0.9.5d)

parts:
  Composant1 = Arduino Micro (Rev3)
  IR1 = TSOP312.., 314.. [package=THT]

nets:
  GND: Composant1.GND, IR1.GND
  N1: Composant1.5V, IR1.Vs
  N2: Composant1.D13_PWM, IR1.Data
